# Fritzing sketch sema2 (saved by Fritzing 0.9.3b)
circuit board: 30.5034cm x 19.1722cm

parts:
  Raspberry_Pi_1 = Raspberry Pi 3 [part_number=RPI-3-V1.2]
  D2F1 = D2F-FL Omron Snap Action Limit Switch with Level
  S5 = Round Pushbutton
  S6 = Round Pushbutton
  M4 = Stepper Motor - Bipolar
  D2F2 = D2F-FL Omron Snap Action Limit Switch with Level
  12V = Power plug
  U1 = L298_BRIDGE_DRIVER [package=powerso20]
  M5 = Stepper Motor - Bipolar
  U2 = L298_BRIDGE_DRIVER [package=powerso20]
  M6 = Stepper Motor - Bipolar
  U3 = L298_BRIDGE_DRIVER [package=powerso20]
  M7 = Stepper Motor - Bipolar
  U4 = L298_BRIDGE_DRIVER [package=powerso20]
  R1 = Resistor [tolerance=±5% resistance=10k package=THT]
  R2 = Resistor [tolerance=±5% resistance=1k package=THT]
  R3 = Resistor [tolerance=±5% resistance=1k package=THT]
  R4 = Resistor [tolerance=±5% resistance=10k package=THT]
  R5 = Resistor [tolerance=±5% resistance=1k package=THT]
  R6 = Resistor [tolerance=±5% resistance=1k package=THT]

nets:
  3V3: Raspberry_Pi_1.3v3, Raspberry_Pi_1.3V3, D2F1.COM, S5.leg1, S6.leg1, D2F2.COM
  N1: Raspberry_Pi_1.GPIO2, U4.IN1
  N2: Raspberry_Pi_1.GPIO3, U4.IN2
  N3: Raspberry_Pi_1.GPIO4, U1.IN1
  GND: Raspberry_Pi_1.GND, 12V.GND, R1.Pin_0, R4.Pin_0
  N4: Raspberry_Pi_1.GPIO17, U1.IN2
  N5: Raspberry_Pi_1.GPIO27, U1.IN3
  N6: Raspberry_Pi_1.GPIO22, U1.IN4
  N7: Raspberry_Pi_1.GPIO5, U2.IN1
  N8: Raspberry_Pi_1.GPIO6, U2.IN2
  N9: Raspberry_Pi_1.GPIO13, U3.IN4
  N10: Raspberry_Pi_1.GPIO19, R5.Pin_0
  N11: Raspberry_Pi_1.GPIO26, R6.Pin_0
  N12: Raspberry_Pi_1.GPIO21, R2.Pin_0
  N13: Raspberry_Pi_1.GPIO20, R3.Pin_0
  N14: Raspberry_Pi_1.GPIO16, U2.IN3
  N15: Raspberry_Pi_1.GPIO12, U2.IN4
  N16: Raspberry_Pi_1.GPIO7, U4.IN3
  N17: Raspberry_Pi_1.GPIO8, U4.IN4
  N18: Raspberry_Pi_1.GPIO25, U3.IN1
  N19: Raspberry_Pi_1.GPIO24, U3.IN2
  N20: Raspberry_Pi_1.GPIO23, U3.IN3
  N21: D2F1.NO, R3.Pin_1, R4.Pin_1
  N22: S5.leg0, R6.Pin_1
  N23: S6.leg0, R5.Pin_1
  N24: M4.A, U1.OUT1
  N25: M4.C, U1.OUT2
  N26: M4.B, U1.OUT3
  N27: M4.D, U1.OUT4
  N28: D2F2.NO, R1.Pin_1, R2.Pin_1
  N29: 12V.VCC, U1.VS
  N30: M5.A, U2.OUT1
  N31: M5.C, U2.OUT2
  N32: M5.B, U2.OUT3
  N33: M5.D, U2.OUT4
  N34: M6.A, U3.OUT1
  N35: M6.C, U3.OUT2, U3.VS
  N36: M6.B, U3.OUT3
  N37: M6.D, U3.OUT4
  N38: M7.A, U4.OUT1
  N39: M7.C, U4.OUT2
  N40: M7.B, U4.OUT3
  N41: M7.D, U4.OUT4

custom parts:
  D2F-FL Omron Snap Action Limit Switch with Level: Snap action switch with stainless steel lever.
